# Fritzing sketch GPS_Proto_Nano (saved by Fritzing 0.9.3b)
breadboards: 2

parts:
  Part1 = Adafruit Ultimate GPS v3 [part_number="Adafruit #746"]
  Part3 = MicroSD Card Module  # not connected
  LED1 = RGB LED (com. cathode, rgb) [package="5 mm [THT]"]
  S2 = SWITCH-MOMENTARY-2 [package=tactile-pth-12mm]
  R1 = Resistor [tolerance=±5% resistance=220 package=THT]
  R2 = Resistor [tolerance=±5% resistance=220 package=THT]
  R3 = Resistor [tolerance=±5% resistance=220 package=THT]
  Part4 = Arduino Nano (Rev3.0)
  S4 = SWITCH-MOMENTARY-2 [package=tactile-pth-12mm]

nets:
  VIN: Part1.VIN, Part4.3V3
  GND: Part1.GND, S2.2, Part4.GND, S4.2
  N1: Part1.RX, Part4.D2
  N2: Part1.TX, Part4.D3
  N3: LED1.red_anode, R1.Pin_0
  N4: LED1.common_cathode, Part4.5V
  N5: LED1.green_anode, R2.Pin_0
  N6: LED1.blue_anode, R3.Pin_0
  N7: S2.1, Part4.RESET
  N8: R1.Pin_1, Part4.D9
  N9: R2.Pin_1, Part4.D6
  N10: R3.Pin_1, Part4.D5
  N11: Part4.D7, S4.1

notes:
  SD Module Pinouts:
  L-R w. pins oriented bottom
  1-GND
  2-Vcc-5v
  3-MISO-12
  4-MOSI-11
  5-SCK-13
  6-CS-10
  |LED|_Com Anode
  R, +5V, G, B
  ** Placement of TX/RX pins on actual GPS module is reversed.

custom parts:
  Adafruit Ultimate GPS v3: We carry a few different GPS modules here in the Adafruit shop, but none that satisfied our every desire - that's why we designed this little GPS breakout board. We believe this is the Ultimate GPS module, so we named it that. It's got everything you want and more: -165 dBm sensitivity, 10 Hz updates, 66 channels 5V friendly design and only 20mA current draw Breadboard friendly + two mounting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
